// Digital circuit BW8cpu.dig as structural Verilog
module BW8cpu (
  input  step,
  input  crystal,
  input  _555,
  input  VCC,
  input  GND,
  input  nREQ,
  input  nNMI,
  input  nIRQ,
  output pass,
  output fail,
  output nACK,
  output D_nC,
  output MEM_nIO,
  output R_nW,
  output [7:0] DATA,
  output [19:0] ADDR,
  output U_nS
);

  wire a_dbus_a, a_dbus_l, a_lhs_a, a_rhs_a, addr_a, addr_inc, addr_xfer_a, alu_dbus_a, alu_op, alu_res,
       b_dbus_a, b_dbus_l, b_lhs_a, b_rhs_a, br_dbus_a, br_dbus_l, c_dbus_a, c_dbus_l, c_lhs_a, c_rhs_a, clk,
       clk_crystal, comparator_1_eq, count, d_dbus_a, d_dbus_l, d_lhs_a, d_rhs_a, da_dbus_a, da_dbus_l,
       dbus_a, dbus_l, dec_sp, dp_dbus_a, dp_dbus_l, ext, io_addr_a, ir_dbus_l, lsb_dbus_a, mem_dbus_a,
       mem_dbus_l, msb_dbus_a, nclk, noffset, not_1_out, not_2_out, not_3_out, not_4_out, not_5_out, nrst,
       nRST_out, off_dbus_l, pc_addr_a, pc_inc, pc_xfer_a, pc_xfer_l, pch_dbus_l, pcl_dbus_l, reg_a, reg_b,
       reg_c, reg_d, reg_da, reg_dp, reg_pc, reg_sp, reg_x, reg_y, reset_1_out, rst, sp_addr_a, sp_inc,
       sp_xfer_a, sp_xfer_l, sph_dbus_l, spl_dbus_l, sr_dbus_a, sr_dbus_l, t_addr_a, th_dbus_a, th_dbus_l,
       th_lhs_a, tl_dbus_a, tl_dbus_l, tl_rhs_a, undriven, x_addr_a, x_inc, x_xfer_a, x_xfer_l, xfer_a,
       xfer_l, xh_dbus_l, xl_dbus_l, y_addr_a, y_inc, y_xfer_a, y_xfer_l, yh_dbus_l, yl_dbus_l;
  wire [2:0] Break_out, clk_mode, t_state;
  wire [4:0] flags;
  wire [7:0] dbus, driver_1_out, driver_2_out, lhs, opcode, reg_off, reg_th, reg_tl, rhs;
  wire [15:0] addr_t;
  wire [17:3] Control_Unit_p20;

  // Probe on dbus
  // Probe on {lhs, rhs}
  // Probe on ADDR
  // Probe on reg_a
  // Probe on reg_b
  // Probe on reg_c
  // Probe on reg_d
  // Probe on reg_dp
  // Probe on reg_da
  // Probe on reg_tl
  // Probe on reg_th
  // Probe C_f on flags[4]
  PowerSupply powersupply_1 (.VDD(VCC), .GND(GND));
  LED led_1 (.in(clk));
  LED led_2 (.in(nrst));
  // Probe Z_f on flags[3]
  // Probe on addr_t
  // Probe on DATA
  // Probe on reg_pc
  // Probe on reg_sp
  // Probe on reg_x
  // Probe on reg_y
  // Probe on reg_off
  // Probe on alu_res
  // Probe N_f on flags[1]
  // Probe V_f on flags[2]
  // Probe I_f on flags[0]
  // Probe on opcode
  // Probe on ext
  Reset reset_1 (.out(reset_1_out));
  Button #(.activeLow("true")) u_nRST (.out(nRST_out));
  Button #(.activeLow("true")) Run (.out(Break_out[0]));
  Button #(.activeLow("true")) Demo (.out(Break_out[1]));
  Button #(.activeLow("true")) Break (.out(Break_out[2]));
  // Probe on flags
  // control_unit Control_Unit: pin names not known; wires that end beside it: nIRQ, opcode, flags, nREQ, nrst, nNMI, 1'b1, clk, dbus_a, dbus_l, alu_op, xfer_a, xfer_l, addr_a, count, dec_sp, nclk, noffset, rst, {Control_Unit_p20[17:16], ext, Control_Unit_p20[14:3], t_state}
  instruction_register Instruction_Register (
    .dbus(dbus), .ndbus_load(ir_dbus_l), .clr(rst), .nclk(nclk), .opcode(opcode));
  memory_bridge Memory_Bridge (.dbus_assert(mem_dbus_a), .dbus_load(mem_dbus_l), .dbus(dbus), .mbus(DATA));
  ROM #(.AddrBits(20), .isProgramMemory("true"), .Bits(8)) ROM (.A(ADDR), .sel(R_nW), .D(DATA));
  and and_1 (nrst, reset_1_out, nRST_out);
  assign dbus = ~msb_dbus_a ? lhs : 8'bz;  // DriverInvSel driverinvsel_1
  assign dbus = ~lsb_dbus_a ? rhs : 8'bz;  // DriverInvSel driverinvsel_2
  // Probe on t_state
  // triple_clock triple_clock_1: pin names not known; wires that end beside it: Break_out, 1'b1, {nrst, 2'b11}, crystal, _555, step, clk, clk_crystal, clk_mode
  // Probe on nclk
  LED Run_Mode_Active (.in(clk_mode[0]));
  LED Demo_Mode_Active (.in(clk_mode[1]));
  LED Break_Mode_Active (.in(clk_mode[2]));
  // Probe on count
  // Probe on dec_sp
  LED cpu (.in(clk));
  LED u_crystal (.in(clk_crystal));
  // Probe on addr_a
  // Probe on xfer_l
  // Probe on xfer_a
  // bus_controller Bus_Controller: pin names not known; wires that end beside it: dbus_a, xfer_l, addr_a, clk, count, dec_sp, nclk, dbus_l, xfer_a, alu_dbus_a, a_dbus_a, b_dbus_a, c_dbus_a, d_dbus_a, dp_dbus_a, da_dbus_a, th_dbus_a, tl_dbus_a, sr_dbus_a, mem_dbus_a, msb_dbus_a, lsb_dbus_a, a_dbus_l, b_dbus_l, c_dbus_l
  // Probe on alu_op
  // Probe on dbus_l
  // Probe on dbus_a
  not not_1 (not_1_out, undriven);
  assign driver_1_out = not_1_out ? dbus : 8'bz;  // Driver driver_1
  assign driver_2_out = not_1_out ? lhs : 8'bz;  // Driver driver_2
  PullDown #(.Bits(8)) pulldown_1 (.out(driver_2_out));
  Comparator #(.Bits(8)) comparator_1 (.a(driver_1_out), .b(driver_2_out), .eq(comparator_1_eq));  // open: gt, lt
  not not_2 (not_2_out, undriven);
  PullDown #(.Bits(8)) pulldown_2 (.out(driver_1_out));
  // alu Arithmetic___Logic_Unit_and_Status_Register: pin names not known; wires that end beside it: alu_op, sr_dbus_l, sr_dbus_a, nclk, rst, lhs, rhs, alu_dbus_a, flags, dbus, alu_res
  // gpr_pair A_and_B: pin names not known; wires that end beside it: a_dbus_l, b_dbus_l, a_dbus_a, b_dbus_a, a_lhs_a, b_lhs_a, a_rhs_a, b_rhs_a, dbus, rst, nclk, reg_a, reg_b, {lhs, rhs}
  // gpr_pair C_and_D: pin names not known; wires that end beside it: mem_dbus_l, ir_dbus_l, off_dbus_l, pch_dbus_l, pcl_dbus_l, sph_dbus_l, spl_dbus_l, xh_dbus_l, xl_dbus_l, c_dbus_l, d_dbus_l, c_dbus_a, d_dbus_a, c_lhs_a, d_lhs_a, c_rhs_a, d_rhs_a, dbus, rst, nclk, reg_c, reg_d, {lhs, rhs}
  // gpr_pair DA_and_DP: pin names not known; wires that end beside it: addr_xfer_a, a_lhs_a, b_lhs_a, c_lhs_a, d_lhs_a, th_lhs_a, a_rhs_a, b_rhs_a, c_rhs_a, dp_dbus_l, da_dbus_l, dp_dbus_a, da_dbus_a, 1'b1, 1'b1, 1'b1, 1'b1, dbus, rst, nclk, reg_dp, reg_da, {lhs, rhs}
  temp_reg_pair temp_reg_pair_1 (
    .nhi_dbus_load(th_dbus_l), .nlo_dbus_load(tl_dbus_l), .nhi_dbus_assert(th_dbus_a),
    .nlo_dbus_assert(tl_dbus_a), .nhi_lhs_assert(th_lhs_a), .nlo_lhs_assert(1'b1), .nhi_rhs_assert(1'b1),
    .nlo_rhs_assert(tl_rhs_a), .dbus(dbus), .clr(rst), .nclk(nclk), .naddr_assert(t_addr_a), .reg_hi(reg_th),
    .reg_lo(reg_tl), .xfer({lhs, rhs}), .addr(addr_t));
  not not_3 (not_3_out, comparator_1_eq);
  and and_2 (pass, comparator_1_eq, not_2_out);
  and and_3 (fail, not_2_out, not_3_out);
  not not_4 (not_4_out, addr_inc);
  not not_5 (not_5_out, nACK);
  // address_register Program_Counter: pin names not known; wires that end beside it: clk, rst, pc_inc, 1'b1, pc_xfer_l, pc_addr_a, pc_xfer_a, pch_dbus_l, pcl_dbus_l, dbus, addr_t, {lhs, rhs}, reg_pc
  // address_register Stack_Pointer: pin names not known; wires that end beside it: clk, rst, sp_inc, 1'b1, sp_xfer_l, sp_addr_a, sp_xfer_a, sph_dbus_l, spl_dbus_l, dbus, addr_t, {lhs, rhs}, reg_sp
  // address_register X_Index: pin names not known; wires that end beside it: clk, rst, x_inc, 1'b1, x_xfer_l, x_addr_a, x_xfer_a, xh_dbus_l, xl_dbus_l, dbus, addr_t, {lhs, rhs}, reg_x
  // address_register Y_Index: pin names not known; wires that end beside it: clk, rst, y_inc, 1'b1, y_xfer_l, y_addr_a, y_xfer_a, yh_dbus_l, yl_dbus_l, dbus, addr_t, {lhs, rhs}, reg_y
  address_offset Address_Bridge (
    .dbus(dbus), .addr_in(addr_t), .noffset_en(noffset), .carry_en(not_4_out),
    .naddr_xfer_assert(addr_xfer_a), .nassert_addr(not_5_out), .clr(rst), .noffset_load(off_dbus_l),
    .nclock(nclk), .R_nW(mem_dbus_l), .MEM_nIO(io_addr_a), .D_nC(pc_addr_a), .nACK(nACK),
    .nload_br(br_dbus_l), .nassert_br(br_dbus_a), .U_nS(1'b0), .UBR_f(1'b0), .addr_out(ADDR),
    .xfer({lhs, rhs}), .q(reg_off), .R_nW_z(R_nW), .MEM_nIO_z(MEM_nIO), .D_nC_z(D_nC));

  assign U_nS = 1'b0;

  // Other names for the same wires on the sheet: ack_addr_a = nACK; addr_out[19:0] = ADDR; clk_cpu = clk;
  //   d_nc_z = D_nC; mbus[7:0] = DATA; mem_nio_z = MEM_nIO; rst_clk_mode[2] = nrst; r_nw_z = R_nW;
  //   xfer[15:0] = {lhs, rhs}

  // Notes on the sheet:
  //   crystal: Hz: 10
  //   VCC: default 1
  //   nREQ: default 1
  //   nNMI: default 1
  //   nIRQ: default 1
  //   External Pinout
  //   Buses & Constants
  //   Registers
  //   CLK
  //   ~RST
  //   ROM loads sim_test.bin
endmodule
